# Fritzing sketch schema (saved by Fritzing 1.0.4)
breadboards: 2

parts:
  Part1 = Arduino Mega 2560 (Rev3)
  LCD1 = LCD screen
  R1 = Resistor [tolerance=±5% resistance=220 power=0W package="1206 [SMD]"]
  RE1 = KY-040 Rotary encoder [package="Breakout board"]
  RE2 = KY-040 Rotary encoder [package="Breakout board"]
  S4 = Pushbutton [package="[THT]"]
  R2 = Basic Force Sensing Resistor (FSR) [package=THT]
  R3 = Resistor [tolerance=±5% resistance=220 power=0W package="0805 [SMD]"]

nets:
  GND: Part1.A2, Part1.GND, LCD1.VSS, LCD1.V0, LCD1.R/W, LCD1.LED-, RE1.GND, RE2.GND, R3.Pin_0
  N1: Part1.D13_PWM, RE1.CLK
  N2: Part1.D12_PWM, RE1.DT
  N3: Part1.D11_PWM, RE2.CLK
  N4: Part1.D10_PWM, RE2.DT
  N5: Part1.D8_PWM, S4.Pin_3, S4.Pin_4
  N6: Part1.D2_PWM, LCD1.DB7
  N7: Part1.D3_PWM, LCD1.DB6
  N8: Part1.D4_PWM, LCD1.DB5
  N9: Part1.D5_PWM, LCD1.DB4
  N10: Part1.D6_PWM, LCD1.E
  N11: Part1.D7_PWM, LCD1.RS
  VCC: Part1.5V, LCD1.VDD, R1.Pin_0, RE1.Vcc, RE2.Vcc, S4.Pin_1, S4.Pin_2, R2.pin_1
  N12: LCD1.LED+, R1.Pin_1
  N13: R2.pin_2, R3.Pin_1

custom parts:
  KY-040 Rotary encoder: KY-040 Rotary Encoder with switch on breakout borad from AZ Delivery
